// Digital circuit D flip-flop.dig as structural Verilog
module D_flip_flop (
  input  D,
  input  CLK,
  output Q,
  output NOT_Q
);

  wire d_switch_1_q, not_1_out;

  D_switch d_switch_1 (.D(D), .CLK(not_1_out), .Q(d_switch_1_q));  // open: nOT_Q
  not not_1 (not_1_out, CLK);
  D_switch d_switch_2 (.D(d_switch_1_q), .CLK(CLK), .Q(Q), .nOT_Q(NOT_Q));
endmodule
