// Digital circuit D latch with clear.dig as structural Verilog
module D_latch_with_clear (
  input  D,
  input  CLK,
  input  CLR,
  output Q,
  output nOT_Q
);

  wire and_1_out, and_2_out, and_3_out, not_1_out, not_2_out, or_1_out;

  not not_1 (not_1_out, CLR);
  and and_1 (and_1_out, D, not_1_out);
  or or_1 (or_1_out, CLK, CLR);
  and and_2 (and_2_out, not_2_out, or_1_out);
  not not_2 (not_2_out, and_1_out);
  and and_3 (and_3_out, and_1_out, or_1_out);
  sr_latch sr_latch_1 (.R(and_2_out), .S(and_3_out), .Q(Q), .NOT_Q(nOT_Q));
endmodule
