// Digital circuit D switch.dig as structural Verilog
module D_switch (
  input  D,
  input  CLK,
  output Q,
  output nOT_Q
);

  wire and_1_out, and_2_out, not_1_out;

  not not_1 (not_1_out, D);
  and and_1 (and_1_out, not_1_out, CLK);
  and and_2 (and_2_out, D, CLK);
  sr_latch sr_latch_1 (.R(and_1_out), .S(and_2_out), .Q(Q), .NOT_Q(nOT_Q));
endmodule
